# Fritzing sketch Diagrama_I2C (saved by Fritzing 0.9.3b)
perfboards: 1

parts:
  Part1 = Arduino Nano (Rev3.0)
  Part2 = Arduino Uno (Rev3)
  4_Channel_Relay1 = 4 Channel Power Relay

nets:
  GND: Part1.GND, Part2.GND, 4_Channel_Relay1.GND
  5V: Part1.5V, Part2.5V, 4_Channel_Relay1.VCC
  N1: Part1.A5, Part2.A5/SCL
  N2: Part1.A4, Part2.A4/SDA
  N3: Part2.D2, 4_Channel_Relay1.IN1
  N4: Part2.D3_PWM, 4_Channel_Relay1.IN2
  N5: Part2.D4, 4_Channel_Relay1.IN3
  N6: Part2.D5_PWM, 4_Channel_Relay1.IN4

custom parts:
  4 Channel Power Relay: A 4 channel power relay. The module operates at 5V.
